# Fritzing sketch Pinguino Board (saved by Fritzing 0.9.2b)
circuit board: 8.8cm x 3.76464cm
breadboards: 1

parts:
  CI = PIC18F2550 [package=dil28-3]
  R1 = Resistor [tolerance=±5% resistance=15k package=THT]
  S1 = Pushbutton [package="[THT]"]
  C1 = Electrolytic Capacitor [capacitance=0.33µF voltage=16V package="100 mil [THT, electrolytic]"]
  Power = LED - 3mm [color="Red (633nm)" package="3 mm [THT]"]
  C2 = Ceramic Capacitor [capacitance=22pF package="100 mil [THT, multilayer]"]
  C3 = Ceramic Capacitor [capacitance=22pF package="100 mil [THT, multilayer]"]
  R2 = Resistor [tolerance=±5% resistance=470 package=THT]
  Run = LED - 3mm [color="Green (570nm)" package="3 mm [THT]"]
  R3 = Resistor [tolerance=±5% resistance=470 package=THT]
  C4 = Capacitor [package=cap-pth-small2]
  Y1 = CRYSTAL [package=hc49us]
  USB = USB Connectors [package=usb-b-pth-vertical]
  J3 = male pin header, 2 pins [form="♂ (male)"]
  J2 = male pin header, 3 pins [form="♂ (male)"]
  J1 = male pin header, 4 pins [form="♂ (male)"]
  J5 = male pin header, 2 pins [form="♂ (male)"]
  J4 = male pin header, 9 pins [form="♂ (male)"]
  Power_plug1 = Power plug
  U1 = Voltage Regulator [package=78xxl]  # not connected
  C5 = Capacitor [package=cap-pth-small2]  # not connected
  JP1 = Header 3 [package=1x03-1mm-ra]  # not connected

nets:
  N1: CI.MCLR_VPP, R1.Pin_1
  N2: CI.RA0_AN0, J1.pin1
  N3: CI.RA1_AN1, J1.pin2
  N4: CI.RA2_AN2, J1.pin3
  N5: CI.RA3_AN3, J1.pin4
  N6: CI.RA4_AN4, R2.Pin_0
  N7: CI.RA5_AN4, J2.pin1
  GND: CI.VSS, S1.Pin_1, S1.Pin_2, C1.-, Power.cathode, C2.1, C3.1, Run.cathode, C4.2, USB.GND, J2.pin2, Power_plug1.GND
  N8: CI.OSC1, J2.pin3
  N9: CI.OSC2, C3.0, Y1.1
  N10: CI.RC0, C2.0, Y1.2
  N11: CI.RC1, J3.pin1
  N12: CI.RC2, J3.pin2
  N13: CI.V-USB, C4.1
  N14: CI.RC4_D-, USB.D-
  N15: CI.RC5_D+, USB.D+
  N16: CI.TX_RC6, J5.pin2
  N17: CI.RX_RC7, J5.pin1
  N18: CI.VDD, R3.Pin_0, USB.VBUS, J4.pin9
  N19: CI.RB0_INT0, J4.pin8
  N20: CI.RB1_INT1_AN10, J4.pin7
  N21: CI.RB2_INT2_AN8, J4.pin6
  N22: CI.RB3_AN9, J4.pin5
  N23: CI.RB4_AN11, J4.pin4
  N24: CI.RB5_PGM, J4.pin3
  N25: CI.RB6_PGC, J4.pin2
  N26: CI.RB7_PGD, J4.pin1
  N27: R1.Pin_0, S1.Pin_3, S1.Pin_4
  N28: C1.+, Power_plug1.VCC
  N29: Power.anode, R3.Pin_1
  N30: R2.Pin_1, Run.anode

notes:
  jumper
  CNP
